# Fritzing sketch qtpyknob (saved by Fritzing 0.9.5d)
circuit board: 8.46667cm x 5.64444cm

parts:
  Part1 = 16 NeoPixel Ring [part_number=1463]
  Part2 = Adafruit QT Py [part_number="Adafruit #4600"]
  ENCODER1 = Rotary Encoder with Knob

nets:
  N1: Part1.IN, Part2.MISO
  VDD: Part1.VDD, Part2.3.3V
  GND: Part1.GND, Part2.GND, ENCODER1.no_name_yet#5
  N2: Part2.A1, ENCODER1.no_name_yet#3
  N3: Part2.A2, ENCODER1.no_name_yet#2
  N4: Part2.A3, ENCODER1.no_name_yet#1
  N5: Part2.MOSI, ENCODER1.no_name_yet#4

custom parts:
  16 NeoPixel Ring: 16 ultra bright smart LED NeoPixels are arranged in a circle with 1.75" (44.5mm) outer diameter. The rings are 'chainable' - connect the output pin of one to the input pin of another. Use only one microcontroller pin to control as many as you can chain together! Each LED is addressable as the driver chip is inside the LED. Each one has ~18mA constant current drive so the color will be very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
  Adafruit QT Py: What a cutie pie! Or is it... a QT Py? This diminutive dev board comes with our favorite lil chip, the SAMD21 (as made famous in our GEMMA M0 and Trinket M0 boards). This time it comes with our favorite connector - the STEMMA QT, a chainable I2C port that can be used with any of our STEMMA QT sensors and accessories. OLEDs! Inertial Measurment Units! Sensors a-plenty. All plug-and-play thanks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
  Rotary Encoder with Knob: Rotary Encoder with 1/4" Shaft and Knob
